# Fritzing sketch Laser Brain Wiring (saved by Fritzing 0.9.3b)
circuit board: 8.46667cm x 5.64444cm
breadboards: 2

parts:
  C3-1 = Ceramic Capacitor [capacitance=1µF voltage=35V package="100 mil [THT, multilayer]"]
  C2-1 = Ceramic Capacitor [capacitance=1µF voltage=35V package="100 mil [THT, multilayer]"]
  C4-1 = Ceramic Capacitor [capacitance=1µF voltage=35V package="100 mil [THT, multilayer]"]
  C1-1 = Ceramic Capacitor [capacitance=1µF voltage=35V package="100 mil [THT, multilayer]"]
  Serial_1_&_2 = RS232 Transceiver [package=dil16]
  Serial_3_&_4 = RS232 Transceiver [package=dil16]
  C1-2 = Ceramic Capacitor [capacitance=1µF voltage=35V package="100 mil [THT, multilayer]"]
  C2-2 = Ceramic Capacitor [capacitance=1µF voltage=35V package="100 mil [THT, multilayer]"]
  C3-2 = Ceramic Capacitor [capacitance=1µF voltage=35V package="100 mil [THT, multilayer]"]
  C4-2 = Ceramic Capacitor [capacitance=1µF voltage=35V package="100 mil [THT, multilayer]"]
  Laser_Triggering = BNC [package=bnc]
  GPIO_BNC1 = BNC [package=bnc]
  GPIO_BNC2 = BNC [package=bnc]
  GPIO_BNC3 = BNC [package=bnc]
  GPIO_BNC4 = BNC [package=bnc]
  Power = Round Pushbutton
  Serial_3 = DB9 Connector For Basic Serial [package=db9]
  Serial_4 = DB9 Connector For Basic Serial [package=db9]
  Serial_1 = DB9 Connector For Basic Serial [package=db9]
  Serial_2 = DB9 Connector For Basic Serial [package=db9]
  Pump_Cap = Ceramic Capacitor [capacitance=1µF voltage=35V package="100 mil [THT, multilayer]"]
  Cancel_Dep = Round Pushbutton
  BeagleBone1 = BeagleBone Black - Labeled Pinout

nets:
  N1: C3-1.0, Serial_1_&_2.V+
  GND: C3-1.1, C4-1.1, Serial_1_&_2.GND, Serial_3_&_4.GND, C3-2.1, C4-2.1, Power.leg1, Serial_3.5, Serial_4.5, Serial_1.5, Serial_2.5, Pump_Cap.0, BeagleBone1.P9_1
  N2: C2-1.0, Serial_1_&_2.C2-
  N3: C2-1.1, Serial_1_&_2.C2+
  N4: C4-1.0, Serial_1_&_2.V-
  N5: C1-1.0, Serial_1_&_2.C1-
  N6: C1-1.1, Serial_1_&_2.C1+
  N7: Serial_1_&_2.T2OUT, Serial_2.3
  N8: Serial_1_&_2.R2IN, Serial_2.2
  N9: Serial_1_&_2.R2OUT, BeagleBone1.P9_22
  N10: Serial_1_&_2.T2IN, BeagleBone1.P9_21
  N11: Serial_1_&_2.T1IN, BeagleBone1.P9_24
  N12: Serial_1_&_2.R1OUT, BeagleBone1.P9_26
  N13: Serial_1_&_2.R1IN, Serial_1.2
  N14: Serial_1_&_2.T1OUT, Serial_1.3
  5V: Serial_1_&_2.VCC, Serial_3_&_4.VCC, Pump_Cap.1, BeagleBone1.P9_7
  N15: Serial_3_&_4.C1+, C1-2.1
  N16: Serial_3_&_4.V+, C3-2.0
  N17: Serial_3_&_4.C1-, C1-2.0
  N18: Serial_3_&_4.C2+, C2-2.1
  N19: Serial_3_&_4.C2-, C2-2.0
  N20: Serial_3_&_4.V-, C4-2.0
  N21: Serial_3_&_4.T2OUT, Serial_4.3
  N22: Serial_3_&_4.R2IN, Serial_4.2
  N23: Serial_3_&_4.R2OUT, BeagleBone1.P9_11
  N24: Serial_3_&_4.T2IN, BeagleBone1.P9_13
  N25: Serial_3_&_4.T1IN, BeagleBone1.P8_37
  N26: Serial_3_&_4.R1OUT, BeagleBone1.P8_38
  N27: Serial_3_&_4.R1IN, Serial_3.2
  N28: Serial_3_&_4.T1OUT, Serial_3.3
  GND_2: Laser_Triggering.GND, GPIO_BNC1.GND, GPIO_BNC2.GND, GPIO_BNC3.GND, GPIO_BNC4.GND, Cancel_Dep.leg0, BeagleBone1.P8_2
  N29: Laser_Triggering.OUT, BeagleBone1.P8_7
  N30: GPIO_BNC1.OUT, BeagleBone1.P8_9
  N31: GPIO_BNC2.OUT, BeagleBone1.P8_11
  N32: GPIO_BNC3.OUT, BeagleBone1.P8_15
  N33: GPIO_BNC4.OUT, BeagleBone1.P8_17
  N34: Power.leg0, BeagleBone1.P9_9
  N35: Cancel_Dep.leg1, BeagleBone1.P8_19

custom parts:
  DB9 Connector For Basic Serial: DB9 Connector Standard DB9 (D-Sub 9) serial connector. Can be used for CAN bus as well as RS485 and RS232. Footprint production proven. Spark Fun Electronics SKU : PRT-00429
  BeagleBone Black - Labeled Pinout: BeagleBone Black rev. A5B
